# Fritzing sketch CouvertureChauffanteSchema2 (saved by Fritzing 0.8.7b)
circuit board: 16.9173cm x 8.05261cm
breadboards: 2

parts:
  LCD1 = LCD screen
  S1 = Pushbutton [package="[THT]"]
  S2 = Pushbutton [package="[THT]"]
  S3 = Pushbutton [package="[THT]"]
  S4 = Pushbutton [package="[THT]"]
  R1 = Resistor [tolerance=±5% resistance=220 package=THT]
  R2 = Resistor [tolerance=±5% resistance=10k package=THT]
  R3 = Resistor [tolerance=±5% resistance=10k package=THT]
  R4 = Resistor [tolerance=±5% resistance=10k package=THT]
  IC1 = 24LC128 [package=THT]
  R5 = Resistor [tolerance=±5% resistance=10k package=THT]
  R6 = Resistor [tolerance=±5% resistance=10k package=THT]
  R11 = Resistor [tolerance=±5% resistance=10k package=THT]
  R12 = Resistor [tolerance=±5% resistance=10k package=THT]
  R13 = Resistor [tolerance=±5% resistance=10k package=THT]
  R14 = Resistor [tolerance=±5% resistance=10k package=THT]
  thRL+ = female pin header, 1 pin [form="♀ (female)"]
  thFR+ = female pin header, 1 pin [form="♀ (female)"]
  thFL+ = female pin header, 1 pin [form="♀ (female)"]
  thFLS = female pin header, 1 pin [form="♀ (female)"]
  thFRS = female pin header, 1 pin [form="♀ (female)"]
  thRLS = female pin header, 1 pin [form="♀ (female)"]
  thRRS = female pin header, 1 pin [form="♀ (female)"]
  pwFL+ = female pin header, 1 pin [form="♀ (female)"]
  pwRL+ = female pin header, 1 pin [form="♀ (female)"]
  pwFR- = female pin header, 1 pin [form="♀ (female)"]
  pwRL- = female pin header, 1 pin [form="♀ (female)"]
  pwFR+ = female pin header, 1 pin [form="♀ (female)"]
  pwRR- = female pin header, 1 pin [form="♀ (female)"]
  pwRR+ = female pin header, 1 pin [form="♀ (female)"]
  pwFL- = female pin header, 1 pin [form="♀ (female)"]
  trFL = NPN-Transistor [package="TO92 [THT]"]
  trFR = NPN-Transistor [package="TO92 [THT]"]
  thRR+ = female pin header, 1 pin [form="♀ (female)"]
  trRR = NPN-Transistor [package="TO92 [THT]"]
  trRL = NPN-Transistor [package="TO92 [THT]"]
  R15 = Resistor [tolerance=±5% resistance=1k package=THT]
  R16 = Resistor [tolerance=±5% resistance=1k package=THT]
  R17 = Resistor [tolerance=±5% resistance=1k package=THT]
  R18 = Resistor [tolerance=±5% resistance=1k package=THT]
  12V = Screw terminal - 2 pins [package=THT]
  ArduinoNano = Arduino Nano (Rev3.0)

nets:
  VSS: LCD1.VSS, LCD1.R/W, LCD1.LED-, S1.Pin_1, S1.Pin_2, S2.Pin_1, S2.Pin_2, S3.Pin_1, S3.Pin_2, S4.Pin_1, S4.Pin_2, IC1.0V, IC1.WP_-_Write_Protect, R11.Pin_1, R12.Pin_1, R13.Pin_1, R14.Pin_1, pwFL+.pin1, pwRL+.pin1, pwFR-.pin1, pwRL-.pin1, pwFR+.pin1, pwRR-.pin1, pwRR+.pin1, pwFL-.pin1, trFL.C, trFR.C, trRR.C, trRL.C, 12V.pin1, ArduinoNano.GND
  VDD: LCD1.VDD, R1.Pin_1, IC1.+V, R5.Pin_0, R6.Pin_0, thRL+.pin1, thFR+.pin1, thFL+.pin1, thRR+.pin1, ArduinoNano.5V
  N1: LCD1.V0, ArduinoNano.D6
  N2: LCD1.RS, ArduinoNano.D12/MISO
  N3: LCD1.E, ArduinoNano.D11/MOSI
  N4: LCD1.DB4, ArduinoNano.D5
  N5: LCD1.DB5, ArduinoNano.D4
  N6: LCD1.DB6, ArduinoNano.D3
  N7: LCD1.DB7, ArduinoNano.D2
  N8: LCD1.LED+, R1.Pin_0
  N9: S1.Pin_3, S1.Pin_4, R2.Pin_0, R4.Pin_1
  N10: S2.Pin_3, S2.Pin_4, R2.Pin_1, ArduinoNano.A6
  N11: S3.Pin_3, S3.Pin_4, R3.Pin_1, R4.Pin_0
  N12: S4.Pin_3, S4.Pin_4, R3.Pin_0
  N13: IC1.SDA_-_I2C_Data, R6.Pin_1, ArduinoNano.A4
  N14: IC1.SCL_-_I2C_Clock, R5.Pin_1, ArduinoNano.A5
  N15: R11.Pin_0, thFLS.pin1
  N16: R12.Pin_0, thFRS.pin1, ArduinoNano.A3
  N17: R13.Pin_0, thRLS.pin1, ArduinoNano.A2
  N18: R14.Pin_0, thRRS.pin1, ArduinoNano.A1
  N19: trFL.E, trFR.E, trRR.E, trRL.E, 12V.pin2
  N20: trFL.B, R15.Pin_0
  N21: trFR.B, R16.Pin_0
  N22: trRR.B, R18.Pin_0
  N23: trRL.B, R17.Pin_0
  N24: R15.Pin_1, ArduinoNano.D7
  N25: R16.Pin_1, ArduinoNano.D8
  N26: R17.Pin_1, ArduinoNano.D9
  N27: R18.Pin_1, ArduinoNano.D10
