# Fritzing sketch CouvertureChauffanteSchema_NewGen (saved by Fritzing 0.9.4)
circuit board: 13.3497cm x 4.74cm
circuit board: 2.63854cm x 2.9499cm
breadboards: 2

parts:
  R12 = Resistor [tolerance=±5% resistance=10k package=THT]
  R13 = Resistor [tolerance=±5% resistance=10k package=THT]
  R14 = Resistor [tolerance=±5% resistance=10k package=THT]
  R15 = Resistor [tolerance=±5% resistance=2.2k package=THT]
  R16 = Resistor [tolerance=±5% resistance=2.2k package=THT]
  R17 = Resistor [tolerance=±5% resistance=2.2k package=THT]
  R18 = Resistor [tolerance=±5% resistance=2.2k package=THT]
  Arduino_Nano = Arduino Nano (Rev3.0)
  tRL+ = female pin header, 1 pin [form="♀ (female)"]
  pRL+ = female pin header, 1 pin [form="♀ (female)"]
  pRR+ = female pin header, 1 pin [form="♀ (female)"]
  tRR+ = female pin header, 1 pin [form="♀ (female)"]
  pRR- = female pin header, 1 pin [form="♀ (female)"]
  tRRs = female pin header, 1 pin [form="♀ (female)"]
  tRLs = female pin header, 1 pin [form="♀ (female)"]
  pRL- = female pin header, 1 pin [form="♀ (female)"]
  pFL- = female pin header, 1 pin [form="♀ (female)"]
  tFL+ = female pin header, 1 pin [form="♀ (female)"]
  tFLs = female pin header, 1 pin [form="♀ (female)"]
  pFL+ = female pin header, 1 pin [form="♀ (female)"]
  pFR+ = female pin header, 1 pin [form="♀ (female)"]
  tFRs = female pin header, 1 pin [form="♀ (female)"]
  pFR- = female pin header, 1 pin [form="♀ (female)"]
  tFR+ = female pin header, 1 pin [form="♀ (female)"]
  J1 = female pin header, 2 pins [form="♀ (female)"]
  J3 = Power Jack [package=power_jack_pth]
  J6 = female pin header, 4 pins [form="♀ (female)"]
  Dwn = Pushbutton [package="[THT]"]
  Bck = Pushbutton [package="[THT]"]
  Up = Pushbutton [package="[THT]"]
  Val = Pushbutton [package="[THT]"]
  LM340 = Voltage Regulator [package=to220-igo]
  R23 = Resistor [tolerance=±5% resistance=160k package=THT]
  R24 = Resistor [tolerance=±5% resistance=100k package=THT]
  to_charger = female pin header, 5 pins [form="♀ (female)"]
  to_Lipo = female pin header, 5 pins [form="♀ (female)"]
  Charge_IN1 = female pin header, 1 pin [form="♀ (female)"]
  D4 = Rectifier Diode [part_number=1N4001 package="300 mil [THT]"]
  Charge_IN2 = female pin header, 1 pin [form="♀ (female)"]
  trFR = Basic FET P-Channel [part_number=TIP120 package="TO220 [THT]"]
  trRR = Basic FET P-Channel [part_number=TIP120 package="TO220 [THT]"]
  trRL = Basic FET P-Channel [part_number=TIP120 package="TO220 [THT]"]
  trFL = Basic FET P-Channel [part_number=TIP120 package="TO220 [THT]"]
  D5 = Rectifier Diode [part_number=1N4001 package="300 mil [THT]"]
  R11 = Resistor [tolerance=±5% resistance=10k package=THT]
  D6 = Rectifier Diode [part_number=1N4001 package="300 mil [THT]"]
  D7 = Rectifier Diode [part_number=1N4001 package="300 mil [THT]"]
  D8 = Rectifier Diode [part_number=1N4001 package="300 mil [THT]"]

nets:
  N1: R12.Pin_0, Arduino_Nano.A0, tFRs.pin1
  GND: R12.Pin_1, R13.Pin_1, R14.Pin_1, Arduino_Nano.GND, J3.GND, J6.pin2, Dwn.Pin_3, Dwn.Pin_4, Bck.Pin_3, Bck.Pin_4, Up.Pin_3, Up.Pin_4, Val.Pin_3, Val.Pin_4, LM340.GND, R24.Pin_1, trFR.source, trRR.source, trRL.source, trFL.source, R11.Pin_1
  N2: R13.Pin_0, Arduino_Nano.A3, tRLs.pin1
  N3: R14.Pin_0, Arduino_Nano.A2, tRRs.pin1
  N4: R15.Pin_0, trFL.gate
  N5: R15.Pin_1, Arduino_Nano.D9
  N6: R16.Pin_0, trFR.gate
  N7: R16.Pin_1, Arduino_Nano.D10
  N8: R17.Pin_0, trRL.gate
  N9: R17.Pin_1, Arduino_Nano.D7
  N10: R18.Pin_0, trRR.gate
  N11: R18.Pin_1, Arduino_Nano.D8
  N12: Arduino_Nano.D2, Val.Pin_1, Val.Pin_2
  N13: Arduino_Nano.D3, Dwn.Pin_1, Dwn.Pin_2
  N14: Arduino_Nano.D4, Up.Pin_1, Up.Pin_2
  N15: Arduino_Nano.D5, Bck.Pin_1, Bck.Pin_2
  N16: Arduino_Nano.VIN, LM340.OUT
  N17: Arduino_Nano.5V, tRL+.pin1, tRR+.pin1, tFL+.pin1, tFR+.pin1, J6.pin1
  N18: Arduino_Nano.A6, R23.Pin_0, R24.Pin_0
  N19: Arduino_Nano.A5, J6.pin3
  N20: Arduino_Nano.A4, J6.pin4
  N21: Arduino_Nano.A1, tFLs.pin1, R11.Pin_0
  N22: pRL+.pin1, pRR+.pin1, pFL+.pin1, pFR+.pin1, J1.pin2, J3.PWR, D5.cathode, D6.cathode, D7.cathode, D8.cathode
  N23: pRR-.pin1, trRR.drain, D8.anode
  N24: pRL-.pin1, trRL.drain, D7.anode
  N25: pFL-.pin1, trFL.drain, D6.anode
  N26: pFR-.pin1, trFR.drain, D5.anode
  N27: J1.pin1, D4.anode, Charge_IN2.pin1
  N28: LM340.IN, R23.Pin_1, Charge_IN1.pin1, D4.cathode
  N29: to_charger.pin1, to_Lipo.pin5
  N30: to_charger.pin2, to_Lipo.pin4
  N31: to_charger.pin3, to_Lipo.pin3
  N32: to_charger.pin4, to_Lipo.pin2
  N33: to_charger.pin5, to_Lipo.pin1

notes:
  +
  -
  Gnd
  Vin
  SDA
  5v
  SCL
  GND
  Bck
  Up
  Dwn
  Val
